// Logisim project Circuito de soma.circ as structural Verilog: 2 circuits, main circuit main
module main (
  input  A,
  input  B,
  input  VEM_1,
  output VAI_,
  output SOMA
);

  Add_1 add_1_1 (.SOMA(VAI_), .VAI_1(SOMA), .A(A), .B(B), .VEM_1(VEM_1));
endmodule

module Add_1 (
  input  A,
  input  B,
  input  VEM_1,
  output SOMA,
  output VAI_1
);

  wire and_1_out, and_2_out, or_1_out, xor_1_out;

  xor xor_1 (xor_1_out, A, B);
  or or_1 (or_1_out, B, VEM_1);
  and and_1 (and_1_out, or_1_out, A);
  and and_2 (and_2_out, B, VEM_1);
  xor xor_2 (SOMA, xor_1_out, VEM_1);
  or or_2 (VAI_1, and_1_out, and_2_out);
endmodule
