// Logisim project circuito-de-soma.circ as structural Verilog: 3 circuits, main circuit main
module main (
  input  A,
  input  B,
  input  VEM_1,
  output VAI_1,
  output SOMA
);

  Add_1 add_1_1 (.SOMA(SOMA), .VAI_1(VAI_1), .A(A), .B(B), .VEM_1(VEM_1));
endmodule

module Add_1 (
  input  A,
  input  B,
  input  VEM_1,
  output SOMA,
  output VAI_1
);

  wire and_1_out, and_2_out, or_1_out, xor_1_out;

  xor xor_1 (xor_1_out, A, B);
  or or_1 (or_1_out, B, VEM_1);
  and and_1 (and_1_out, or_1_out, A);
  and and_2 (and_2_out, B, VEM_1);
  xor xor_2 (SOMA, xor_1_out, VEM_1);
  or or_2 (VAI_1, and_1_out, and_2_out);
endmodule

module Add_4 (
  input  [3:0] B,
  input  [3:0] A,
  output Overflow,
  output [3:0] out_4
);

  wire add_1_2_vai_1, add_1_3_vai_1, add_1_4_vai_1;

  // Probe on A
  Add_1 add_1_1 (.SOMA(out_4[3]), .VAI_1(Overflow), .A(A[3]), .B(B[3]), .VEM_1(add_1_3_vai_1));
  Add_1 add_1_2 (.SOMA(out_4[1]), .VAI_1(add_1_2_vai_1), .A(A[1]), .B(B[1]), .VEM_1(add_1_4_vai_1));
  Add_1 add_1_3 (.SOMA(out_4[2]), .VAI_1(add_1_3_vai_1), .A(A[2]), .B(B[2]), .VEM_1(add_1_2_vai_1));
  // Probe on out_4
  Add_1 add_1_4 (.SOMA(out_4[0]), .VAI_1(add_1_4_vai_1), .A(A[0]), .B(B[0]), .VEM_1(1'b0));
  // Probe on B
endmodule
